# Fritzing sketch circuit_diagram_no_V2 (saved by Fritzing 0.9.4)
breadboards: 1

parts:
  Raspberry_Pi_1 = Raspberry Pi 3 [part_number=RPI-3-V1.2]
  Part1 = Arduino Uno (Rev3)
  Q1 = NPN-Transistor [package="TO92 [THT]"]
  Q3 = NPN-Transistor [package="TO92 [THT]"]
  R3 = Resistor [tolerance=±5% resistance=1M package=THT]
  R4 = Resistor [tolerance=±5% resistance=1M package=THT]
  R5 = Resistor [tolerance=±5% resistance=1M package=THT]
  Q4 = NPN-Transistor [package="TO92 [THT]"]
  R6 = Resistor [tolerance=±5% resistance=1M package=THT]
  S1 = Pushbutton [package="[THT]"]
  S2 = Pushbutton [package="[THT]"]
  Q5 = NPN-Transistor [package="TO92 [THT]"]
  Q6 = NPN-Transistor [package="TO92 [THT]"]
  Q7 = NPN-Transistor [package="TO92 [THT]"]

nets:
  GND: Raspberry_Pi_1.GND, Part1.GND, Q3.C, Q4.C, Q5.E, Q6.E, Q7.E
  N1: Raspberry_Pi_1.GPIO17, Q3.E
  N2: Raspberry_Pi_1.GPIO26, Q5.B
  N3: Raspberry_Pi_1.GPIO21, Q6.B
  N4: Raspberry_Pi_1.GPIO23, Q4.E
  N5: Raspberry_Pi_1.GPIO18, Q1.E
  N6: Part1.D8, R6.Pin_0
  N7: Part1.D9_PWM, R4.Pin_0
  N8: Part1.D3_PWM, Q6.C
  N9: Part1.D4, S2.Pin_3, S2.Pin_4
  N10: Part1.D5_PWM, S1.Pin_3, S1.Pin_4
  N11: Q1.B, R3.Pin_1
  N12: Q3.B, R5.Pin_1
  N13: R4.Pin_1, Q7.B
  N14: Q4.B, R6.Pin_1
  N15: S1.Pin_1, S1.Pin_2
  N16: S2.Pin_1, S2.Pin_2
